// Logisim project ALU.circ as structural Verilog: 1 circuit, main circuit ALU
module ALU (
  input  B7,
  input  B6,
  input  B5,
  input  B4,
  input  B3,
  input  B2,
  input  B1,
  input  B0,
  input  A7,
  input  A6,
  input  A5,
  input  A4,
  input  A3,
  input  A2,
  input  A1,
  input  A0,
  input  ENB,
  input  ENA,
  input  INVA,
  input  Carry_In,
  input  F1,
  input  F0,
  input  Clk,
  output Carry_Out,
  output C7,
  output C6,
  output C5,
  output C4,
  output C3,
  output C2,
  output C1,
  output C0
);

  wire n2to4decoder_1_a___b, n2to4decoder_1_a___not_b, n2to4decoder_1_not_a___b,
       n2to4decoder_1_not_a___not_b, not_1_out, not_2_out, not_3_out;
  wire [7:0] controlled_buffer_1_out, controlled_buffer_4_out, controlled_buffer_7_out,
       n8_bit_bitwise_and_1__00, n8_bit_bitwise_or_1__00, n8bitripplecarryadder_1_out_26, N__00;

  not not_1 (not_1_out, ENB);
  assign controlled_buffer_1_out = not_1_out ? {8{ENB}} : 8'bz;  // Controlled_Buffer controlled_buffer_1
  _8_bit_Bitwise_AND u_8_bit_bitwise_and_1 (
    .A7(controlled_buffer_7_out[7]), .A6(controlled_buffer_7_out[6]), .A5(controlled_buffer_7_out[5]),
    .A4(controlled_buffer_7_out[4]), .A3(controlled_buffer_7_out[3]), .A2(controlled_buffer_7_out[2]),
    .A1(controlled_buffer_7_out[1]), .A0(controlled_buffer_7_out[0]), .B7(controlled_buffer_1_out[7]),
    .B6(controlled_buffer_1_out[6]), .B5(controlled_buffer_1_out[5]), .B4(controlled_buffer_1_out[4]),
    .B3(controlled_buffer_1_out[3]), .B2(controlled_buffer_1_out[2]), .B1(controlled_buffer_1_out[1]),
    .B0(controlled_buffer_1_out[0]), ._07(n8_bit_bitwise_and_1__00[7]), ._06(n8_bit_bitwise_and_1__00[6]),
    ._05(n8_bit_bitwise_and_1__00[5]), ._04(n8_bit_bitwise_and_1__00[4]), ._03(n8_bit_bitwise_and_1__00[3]),
    ._02(n8_bit_bitwise_and_1__00[2]), ._01(n8_bit_bitwise_and_1__00[1]), ._00(n8_bit_bitwise_and_1__00[0]));
  _2to4Decoder u_2to4decoder_1 (
    .A(F1), .B(F0), .Enable(Clk), .NOT_A___NOT_B(n2to4decoder_1_not_a___not_b),
    .A___NOT_B(n2to4decoder_1_a___not_b), .NOT_A___B(n2to4decoder_1_not_a___b), .A___B(n2to4decoder_1_a___b));
  assign controlled_buffer_1_out = ENB ? {B7, B6, B5, B4, B3, B2, B1, B0} : 8'bz;  // Controlled_Buffer controlled_buffer_2
  assign {C7, C6, C5, C4, C3, C2, C1, C0} = n2to4decoder_1_not_a___not_b ? n8_bit_bitwise_and_1__00 : 8'bz;  // Controlled_Buffer controlled_buffer_3
  assign controlled_buffer_4_out = not_2_out ? {8{ENA}} : 8'bz;  // Controlled_Buffer controlled_buffer_4
  not not_2 (not_2_out, ENA);
  _8_bit_Bitwise_OR u_8_bit_bitwise_or_1 (
    .A7(controlled_buffer_7_out[7]), .A6(controlled_buffer_7_out[6]), .A5(controlled_buffer_7_out[5]),
    .A4(controlled_buffer_7_out[4]), .A3(controlled_buffer_7_out[3]), .A2(controlled_buffer_7_out[2]),
    .A1(controlled_buffer_7_out[1]), .A0(controlled_buffer_7_out[0]), .B7(controlled_buffer_1_out[7]),
    .B6(controlled_buffer_1_out[6]), .B5(controlled_buffer_1_out[5]), .B4(controlled_buffer_1_out[4]),
    .B3(controlled_buffer_1_out[3]), .B2(controlled_buffer_1_out[2]), .B1(controlled_buffer_1_out[1]),
    .B0(controlled_buffer_1_out[0]), ._07(n8_bit_bitwise_or_1__00[7]), ._06(n8_bit_bitwise_or_1__00[6]),
    ._05(n8_bit_bitwise_or_1__00[5]), ._04(n8_bit_bitwise_or_1__00[4]), ._03(n8_bit_bitwise_or_1__00[3]),
    ._02(n8_bit_bitwise_or_1__00[2]), ._01(n8_bit_bitwise_or_1__00[1]), ._00(n8_bit_bitwise_or_1__00[0]));
  assign {C7, C6, C5, C4, C3, C2, C1, C0} = n2to4decoder_1_a___not_b ? n8_bit_bitwise_or_1__00 : 8'bz;  // Controlled_Buffer controlled_buffer_5
  assign controlled_buffer_4_out = ENA ? {A7, A6, A5, A4, A3, A2, A1, A0} : 8'bz;  // Controlled_Buffer controlled_buffer_6
  not not_3 (not_3_out, INVA);
  assign controlled_buffer_7_out = not_3_out ? controlled_buffer_4_out : 8'bz;  // Controlled_Buffer controlled_buffer_7
  _8_bit_Bitwise_NOT N (
    .A7(controlled_buffer_1_out[7]), .A6(controlled_buffer_1_out[6]), .A5(controlled_buffer_1_out[5]),
    .A4(controlled_buffer_1_out[4]), .A3(controlled_buffer_1_out[3]), .A2(controlled_buffer_1_out[2]),
    .A1(controlled_buffer_1_out[1]), .A0(controlled_buffer_1_out[0]), ._07(N__00[7]), ._06(N__00[6]),
    ._05(N__00[5]), ._04(N__00[4]), ._03(N__00[3]), ._02(N__00[2]), ._01(N__00[1]), ._00(N__00[0]));
  assign controlled_buffer_7_out = INVA ? ~controlled_buffer_4_out : 8'bz;  // Controlled_Inverter controlled_inverter_1
  assign {C7, C6, C5, C4, C3, C2, C1, C0} = n2to4decoder_1_not_a___b ? N__00 : 8'bz;  // Controlled_Buffer controlled_buffer_8
  _8bitRippleCarryAdder u_8bitripplecarryadder_1 (
    .C_out(Carry_Out), .A7(controlled_buffer_1_out[7]), .A6(controlled_buffer_1_out[6]),
    .A5(controlled_buffer_1_out[5]), .A4(controlled_buffer_1_out[4]), .A3(controlled_buffer_1_out[3]),
    .A2(controlled_buffer_1_out[2]), .A1(controlled_buffer_1_out[1]), .A0(controlled_buffer_1_out[0]),
    .B7(controlled_buffer_7_out[7]), .B6(controlled_buffer_7_out[6]), .B5(controlled_buffer_7_out[5]),
    .B4(controlled_buffer_7_out[4]), .B3(controlled_buffer_7_out[3]), .B2(controlled_buffer_7_out[2]),
    .B1(controlled_buffer_7_out[1]), .B0(controlled_buffer_7_out[0]),
    .out_19(n8bitripplecarryadder_1_out_26[7]), .out_20(n8bitripplecarryadder_1_out_26[6]),
    .out_21(n8bitripplecarryadder_1_out_26[5]), .out_22(n8bitripplecarryadder_1_out_26[4]),
    .out_23(n8bitripplecarryadder_1_out_26[3]), .out_24(n8bitripplecarryadder_1_out_26[2]),
    .out_25(n8bitripplecarryadder_1_out_26[1]), .out_26(n8bitripplecarryadder_1_out_26[0]), .C_in(Carry_In));
  assign {C7, C6, C5, C4, C3, C2, C1, C0} = n2to4decoder_1_a___b ? n8bitripplecarryadder_1_out_26 : 8'bz;  // Controlled_Buffer controlled_buffer_9

  // Notes on the sheet:
  //   AND
  //   Dec
  //   Input B
  //   OR
  //   NOT
  //   Input A
  //   Ripple  Adder
endmodule
