// Logisim project AdderCircuits.circ as structural Verilog: 3 circuits, main circuit halfAdder
module halfAdder (
  input  A,
  input  B,
  output S,
  output C
);

  xor xor_1 (S, A, B);
  and and_1 (C, A, B);
endmodule

module fullAdder (
  input  A,
  input  B,
  input  C_in,
  output C_out,
  output S
);

  wire halfadder_1_c, halfadder_1_s, halfadder_2_c;

  halfAdder halfadder_1 (.A(A), .B(B), .S(halfadder_1_s), .C(halfadder_1_c));
  halfAdder halfadder_2 (.A(halfadder_1_s), .B(C_in), .S(S), .C(halfadder_2_c));
  or or_1 (C_out, halfadder_2_c, halfadder_1_c);
endmodule

module _8bitRippleCarryAdder (
  input  A7,
  input  A6,
  input  A5,
  input  A4,
  input  A3,
  input  A2,
  input  A1,
  input  A0,
  input  B7,
  input  B6,
  input  B5,
  input  B4,
  input  B3,
  input  B2,
  input  B1,
  input  B0,
  input  C_in,
  output C_out,
  output out_19,
  output out_20,
  output out_21,
  output out_22,
  output out_23,
  output out_24,
  output out_25,
  output out_26
);

  wire fulladder_2_c_out, fulladder_3_c_out, fulladder_4_c_out, fulladder_5_c_out, fulladder_6_c_out,
       fulladder_7_c_out, fulladder_8_c_out;

  fullAdder fulladder_1 (.C_out(C_out), .C_in(fulladder_2_c_out), .A(A7), .B(B7), .S(out_19));
  fullAdder fulladder_2 (.C_out(fulladder_2_c_out), .C_in(fulladder_3_c_out), .A(A6), .B(B6), .S(out_20));
  fullAdder fulladder_3 (.C_out(fulladder_3_c_out), .C_in(fulladder_4_c_out), .A(A5), .B(B5), .S(out_21));
  fullAdder fulladder_4 (.C_out(fulladder_4_c_out), .C_in(fulladder_5_c_out), .A(A4), .B(B4), .S(out_22));
  fullAdder fulladder_5 (.C_out(fulladder_5_c_out), .C_in(fulladder_6_c_out), .A(A3), .B(B3), .S(out_23));
  fullAdder fulladder_6 (.C_out(fulladder_6_c_out), .C_in(fulladder_7_c_out), .A(A2), .B(B2), .S(out_24));
  fullAdder fulladder_7 (.C_out(fulladder_7_c_out), .C_in(fulladder_8_c_out), .A(A1), .B(B1), .S(out_25));
  fullAdder fulladder_8 (.C_out(fulladder_8_c_out), .C_in(C_in), .A(A0), .B(B0), .S(out_26));
endmodule
