// Logisim project Bitwise Functions.circ as structural Verilog: 4 circuits, main circuit main
module main (
);

  _8_bit_Bitwise_AND u_8_bit_bitwise_and_1 ();  // open: A7, A6, A5, A4, A3, A2, A1, A0, B7, B6, B5, B4, B3, B2, B1, B0, _07, _06, _05, _04, _03, _02, _01, _00
  _8_bit_Bitwise_NOT u_8_bit_bitwise_not_1 ();  // open: A7, A6, A5, A4, A3, A2, A1, A0, _07, _06, _05, _04, _03, _02, _01, _00
  _8_bit_Bitwise_OR u_8_bit_bitwise_or_1 ();  // open: A7, A6, A5, A4, A3, A2, A1, A0, B7, B6, B5, B4, B3, B2, B1, B0, _07, _06, _05, _04, _03, _02, _01, _00
endmodule

module _8_bit_Bitwise_AND (
  input  A7,
  input  A6,
  input  A5,
  input  A4,
  input  A3,
  input  A2,
  input  A1,
  input  A0,
  input  B7,
  input  B6,
  input  B5,
  input  B4,
  input  B3,
  input  B2,
  input  B1,
  input  B0,
  output _07,
  output _06,
  output _05,
  output _04,
  output _03,
  output _02,
  output _01,
  output _00
);

  and _7 (_07, A7, B7);
  and _6 (_06, A6, B6);
  and _5 (_05, A5, B5);
  and _4 (_04, A4, B4);
  and _3 (_03, A3, B3);
  and _2 (_02, A2, B2);
  and _1 (_01, A1, B1);
  and _0 (_00, A0, B0);

  // Notes on the sheet:
  //   Input A
  //   Input B
  //   Output
endmodule

module _8_bit_Bitwise_OR (
  input  A7,
  input  A6,
  input  A5,
  input  A4,
  input  A3,
  input  A2,
  input  A1,
  input  A0,
  input  B7,
  input  B6,
  input  B5,
  input  B4,
  input  B3,
  input  B2,
  input  B1,
  input  B0,
  output _07,
  output _06,
  output _05,
  output _04,
  output _03,
  output _02,
  output _01,
  output _00
);

  or _7 (_07, A7, B7);
  or _6 (_06, A6, B6);
  or _5 (_05, A5, B5);
  or _4 (_04, A4, B4);
  or _3 (_03, A3, B3);
  or _2 (_02, A2, B2);
  or _1 (_01, A1, B1);
  or _0 (_00, A0, B0);

  // Notes on the sheet:
  //   Input A
  //   Input B
  //   Output
endmodule

module _8_bit_Bitwise_NOT (
  input  A7,
  input  A6,
  input  A5,
  input  A4,
  input  A3,
  input  A2,
  input  A1,
  input  A0,
  output _07,
  output _06,
  output _05,
  output _04,
  output _03,
  output _02,
  output _01,
  output _00
);

  not not_1 (_07, A7);
  not not_2 (_06, A6);
  not not_3 (_05, A5);
  not not_4 (_04, A4);
  not not_5 (_03, A3);
  not not_6 (_02, A2);
  not not_7 (_01, A1);
  not not_8 (_00, A0);

  // Notes on the sheet:
  //   Input
  //   Output
endmodule
