// Logisim project BuildingBlocks.circ as structural Verilog: 4 circuits, main circuit 2to4Decoder
module _2to4Decoder (
  input  A,
  input  B,
  input  Enable,
  output NOT_A___NOT_B,
  output A___NOT_B,
  output NOT_A___B,
  output A___B
);

  wire not_1_out, not_2_out;

  not not_1 (not_1_out, A);
  not not_2 (not_2_out, B);
  and _00 (NOT_A___NOT_B, not_1_out, not_2_out, Enable);
  and _01 (A___NOT_B, A, not_2_out, Enable);
  and _10 (NOT_A___B, B, not_1_out, Enable);
  and _11 (A___B, B, A, Enable);
endmodule

module _8to1Multiplexer (
  input  D0,
  input  D1,
  input  D2,
  input  D3,
  input  D4,
  input  D5,
  input  D6,
  input  D7,
  input  A,
  input  B,
  input  C,
  output F
);

  wire and_1_out, and_2_out, and_3_out, and_4_out, and_5_out, and_6_out, and_7_out, and_8_out, not_1_out,
       not_2_out, NOT_A_out;

  not NOT_A (NOT_A_out, A);
  not not_1 (not_1_out, B);
  not not_2 (not_2_out, C);
  and and_1 (and_1_out, D0, NOT_A_out, not_1_out, not_2_out);
  and and_2 (and_2_out, D1, NOT_A_out, not_1_out, C);
  and and_3 (and_3_out, D2, NOT_A_out, B, not_2_out);
  and and_4 (and_4_out, D3, NOT_A_out, B, C);
  and and_5 (and_5_out, D4, A, not_1_out, not_2_out);
  and and_6 (and_6_out, D5, A, not_1_out, C);
  and and_7 (and_7_out, D6, A, B, not_2_out);
  and and_8 (and_8_out, D7, A, B, C);
  or or_1 (F, and_1_out, and_2_out, and_3_out, and_4_out, and_5_out, and_6_out, and_7_out, and_8_out);
  _2to4Decoder u_2to4decoder_1 ();  // open: A, B, Enable, NOT_A___NOT_B, A___NOT_B, NOT_A___B, A___B
endmodule

module _8_Bit_Comparator (
  input  A7,
  input  A6,
  input  A5,
  input  A4,
  input  A3,
  input  A2,
  input  A1,
  input  A0,
  input  B7,
  input  B6,
  input  B5,
  input  B4,
  input  B3,
  input  B2,
  input  B1,
  input  B0,
  output X
);

  wire xnor_1_out, xnor_2_out, xnor_3_out, xnor_4_out, xnor_5_out, xnor_6_out, xnor_7_out, xnor_8_out;

  xnor xnor_1 (xnor_1_out, A0, B0);
  xnor xnor_2 (xnor_2_out, A1, B1);
  xnor xnor_3 (xnor_3_out, A2, B2);
  xnor xnor_4 (xnor_4_out, A3, B3);
  xnor xnor_5 (xnor_5_out, A4, B4);
  xnor xnor_6 (xnor_6_out, A5, B5);
  xnor xnor_7 (xnor_7_out, A6, B6);
  not xnor_8 (xnor_8_out, A7);  // XNOR_Gate
  and and_1 (X, xnor_1_out, xnor_2_out, xnor_3_out, xnor_4_out, xnor_5_out, xnor_6_out, xnor_7_out, xnor_8_out);
endmodule

module _8_Bit_wide__1_bit_Left_Right_Shifter (
  input  D0,
  input  D1,
  input  D2,
  input  D3,
  input  D4,
  input  D5,
  input  D6,
  input  D7,
  input  C,
  output S0,
  output S1,
  output S2,
  output S3,
  output S4,
  output S5,
  output S6,
  output S7
);

  wire and_1_out, and_3_out, and_4_out, and_5_out, and_6_out, and_7_out, and_8_out, and_9_out, and_10_out,
       and_11_out, and_13_out, and_14_out, not_1_out;

  not not_1 (not_1_out, C);
  and and_1 (and_1_out, D0, C);
  and and_2 (S0, not_1_out, D1);
  or or_1 (S1, and_1_out, and_5_out);
  and and_3 (and_3_out, D1, C);
  and and_4 (and_4_out, D2, C);
  and and_5 (and_5_out, not_1_out, D2);
  or or_2 (S2, and_3_out, and_6_out);
  and and_6 (and_6_out, not_1_out, D3);
  or or_3 (S3, and_4_out, and_9_out);
  and and_7 (and_7_out, D3, C);
  and and_8 (and_8_out, D4, C);
  and and_9 (and_9_out, not_1_out, D4);
  or or_4 (S4, and_7_out, and_10_out);
  and and_10 (and_10_out, not_1_out, D5);
  or or_5 (S5, and_8_out, and_13_out);
  and and_11 (and_11_out, D5, C);
  and and_12 (S7, D6, C);
  and and_13 (and_13_out, not_1_out, D6);
  or or_6 (S6, and_11_out, and_14_out);
  and and_14 (and_14_out, not_1_out, D7);
endmodule
