// Logisim project CPU.circ as structural Verilog: 1 circuit, main circuit CPU
module CPU (
  input  [7:0] in_1,
  input  Clk,
  input  Fetch,
  input  MAR,
  input  MDR,
  input  PC,
  input  MBR,
  input  SP,
  input  LV,
  input  CPP,
  input  TOS,
  input  OPC,
  input  H,
  input  ENB,
  input  ENA,
  input  INVA,
  input  Cin,
  input  F1,
  input  F0,
  input  [2:0] B_Bus,
  input  LRS,
  input  ENS,
  output [7:0] out_23,
  output [7:0] out_24,
  output Carry_out
);

  wire and_1_out, and_2_out, and_3_out, and_4_out, and_5_out, and_6_out, and_7_out, and_8_out, and_9_out,
       and_10_out, decoder_1_out0, decoder_1_out1, decoder_1_out2, decoder_1_out3, decoder_1_out4,
       decoder_1_out5, decoder_1_out6, decoder_1_out7, n8_bit_register_10_q0, n8_bit_register_10_q1,
       n8_bit_register_10_q2, n8_bit_register_10_q3, n8_bit_register_10_q4, n8_bit_register_10_q5,
       n8_bit_register_10_q6, n8_bit_register_10_q7, not_1_out, not_2_out;
  wire [7:0] alu_1_c0, controlled_buffer_1_out, controlled_buffer_2_out, controlled_buffer_4_out,
       controlled_buffer_5_out, controlled_buffer_6_out, controlled_buffer_7_out, controlled_buffer_8_out,
       controlled_buffer_9_out, controlled_buffer_10_out, controlled_buffer_11_out, controlled_buffer_12_out,
       controlled_buffer_13_out, controlled_buffer_21_out, controlled_buffer_22_out, n8_bit_register_3_q0,
       n8_bit_register_4_q0, n8_bit_register_5_q0, n8_bit_register_6_q0, n8_bit_register_7_q0,
       n8_bit_register_8_q0, n8_bit_register_9_q0, n8_bit_wide_1_bit_left_right_shifter_1_s0;

  assign controlled_buffer_1_out = Fetch ? in_1 : 8'bz;  // Controlled_Buffer controlled_buffer_1
  not not_1 (not_1_out, Fetch);
  assign controlled_buffer_2_out = and_1_out ? controlled_buffer_22_out : 8'bz;  // Controlled_Buffer controlled_buffer_2
  assign controlled_buffer_1_out = not_1_out ? controlled_buffer_22_out : 8'bz;  // Controlled_Buffer controlled_buffer_3
  and and_1 (and_1_out, Clk, MAR);
  assign controlled_buffer_4_out = and_3_out ? controlled_buffer_1_out : 8'bz;  // Controlled_Buffer controlled_buffer_4
  assign controlled_buffer_5_out = and_2_out ? controlled_buffer_22_out : 8'bz;  // Controlled_Buffer controlled_buffer_5
  assign controlled_buffer_6_out = and_4_out ? controlled_buffer_22_out : 8'bz;  // Controlled_Buffer controlled_buffer_6
  assign controlled_buffer_7_out = and_6_out ? controlled_buffer_22_out : 8'bz;  // Controlled_Buffer controlled_buffer_7
  and and_2 (and_2_out, Clk, PC);
  and and_3 (and_3_out, Clk, MDR);
  and and_4 (and_4_out, Clk, MBR);
  assign controlled_buffer_8_out = and_7_out ? controlled_buffer_22_out : 8'bz;  // Controlled_Buffer controlled_buffer_8
  assign controlled_buffer_9_out = and_5_out ? controlled_buffer_22_out : 8'bz;  // Controlled_Buffer controlled_buffer_9
  assign controlled_buffer_10_out = and_8_out ? controlled_buffer_22_out : 8'bz;  // Controlled_Buffer controlled_buffer_10
  assign controlled_buffer_11_out = and_9_out ? controlled_buffer_22_out : 8'bz;  // Controlled_Buffer controlled_buffer_11
  and and_5 (and_5_out, Clk, CPP);
  and and_6 (and_6_out, Clk, SP);
  and and_7 (and_7_out, Clk, LV);
  _8_bit_register u_8_bit_register_1 (
    .CLK(and_1_out), .D7(controlled_buffer_2_out[7]), .D6(controlled_buffer_2_out[6]),
    .D5(controlled_buffer_2_out[5]), .D4(controlled_buffer_2_out[4]), .D3(controlled_buffer_2_out[3]),
    .D2(controlled_buffer_2_out[2]), .D1(controlled_buffer_2_out[1]), .D0(controlled_buffer_2_out[0]),
    .Q7(out_23[7]), .Q6(out_23[6]), .Q5(out_23[5]), .Q4(out_23[4]), .Q3(out_23[3]), .Q2(out_23[2]),
    .Q1(out_23[1]), .Q0(out_23[0]));
  _8_bit_register u_8_bit_register_2 (
    .CLK(and_3_out), .D7(controlled_buffer_4_out[7]), .D6(controlled_buffer_4_out[6]),
    .D5(controlled_buffer_4_out[5]), .D4(controlled_buffer_4_out[4]), .D3(controlled_buffer_4_out[3]),
    .D2(controlled_buffer_4_out[2]), .D1(controlled_buffer_4_out[1]), .D0(controlled_buffer_4_out[0]),
    .Q7(out_24[7]), .Q6(out_24[6]), .Q5(out_24[5]), .Q4(out_24[4]), .Q3(out_24[3]), .Q2(out_24[2]),
    .Q1(out_24[1]), .Q0(out_24[0]));
  _8_bit_register u_8_bit_register_3 (
    .CLK(and_2_out), .D7(controlled_buffer_5_out[7]), .D6(controlled_buffer_5_out[6]),
    .D5(controlled_buffer_5_out[5]), .D4(controlled_buffer_5_out[4]), .D3(controlled_buffer_5_out[3]),
    .D2(controlled_buffer_5_out[2]), .D1(controlled_buffer_5_out[1]), .D0(controlled_buffer_5_out[0]),
    .Q7(n8_bit_register_3_q0[7]), .Q6(n8_bit_register_3_q0[6]), .Q5(n8_bit_register_3_q0[5]),
    .Q4(n8_bit_register_3_q0[4]), .Q3(n8_bit_register_3_q0[3]), .Q2(n8_bit_register_3_q0[2]),
    .Q1(n8_bit_register_3_q0[1]), .Q0(n8_bit_register_3_q0[0]));
  _8_bit_register u_8_bit_register_4 (
    .CLK(and_4_out), .D7(controlled_buffer_6_out[7]), .D6(controlled_buffer_6_out[6]),
    .D5(controlled_buffer_6_out[5]), .D4(controlled_buffer_6_out[4]), .D3(controlled_buffer_6_out[3]),
    .D2(controlled_buffer_6_out[2]), .D1(controlled_buffer_6_out[1]), .D0(controlled_buffer_6_out[0]),
    .Q7(n8_bit_register_4_q0[7]), .Q6(n8_bit_register_4_q0[6]), .Q5(n8_bit_register_4_q0[5]),
    .Q4(n8_bit_register_4_q0[4]), .Q3(n8_bit_register_4_q0[3]), .Q2(n8_bit_register_4_q0[2]),
    .Q1(n8_bit_register_4_q0[1]), .Q0(n8_bit_register_4_q0[0]));
  _8_bit_register u_8_bit_register_5 (
    .CLK(and_6_out), .D7(controlled_buffer_7_out[7]), .D6(controlled_buffer_7_out[6]),
    .D5(controlled_buffer_7_out[5]), .D4(controlled_buffer_7_out[4]), .D3(controlled_buffer_7_out[3]),
    .D2(controlled_buffer_7_out[2]), .D1(controlled_buffer_7_out[1]), .D0(controlled_buffer_7_out[0]),
    .Q7(n8_bit_register_5_q0[7]), .Q6(n8_bit_register_5_q0[6]), .Q5(n8_bit_register_5_q0[5]),
    .Q4(n8_bit_register_5_q0[4]), .Q3(n8_bit_register_5_q0[3]), .Q2(n8_bit_register_5_q0[2]),
    .Q1(n8_bit_register_5_q0[1]), .Q0(n8_bit_register_5_q0[0]));
  _8_bit_register u_8_bit_register_6 (
    .CLK(and_7_out), .D7(controlled_buffer_8_out[7]), .D6(controlled_buffer_8_out[6]),
    .D5(controlled_buffer_8_out[5]), .D4(controlled_buffer_8_out[4]), .D3(controlled_buffer_8_out[3]),
    .D2(controlled_buffer_8_out[2]), .D1(controlled_buffer_8_out[1]), .D0(controlled_buffer_8_out[0]),
    .Q7(n8_bit_register_6_q0[7]), .Q6(n8_bit_register_6_q0[6]), .Q5(n8_bit_register_6_q0[5]),
    .Q4(n8_bit_register_6_q0[4]), .Q3(n8_bit_register_6_q0[3]), .Q2(n8_bit_register_6_q0[2]),
    .Q1(n8_bit_register_6_q0[1]), .Q0(n8_bit_register_6_q0[0]));
  _8_bit_register u_8_bit_register_7 (
    .CLK(and_5_out), .D7(controlled_buffer_9_out[7]), .D6(controlled_buffer_9_out[6]),
    .D5(controlled_buffer_9_out[5]), .D4(controlled_buffer_9_out[4]), .D3(controlled_buffer_9_out[3]),
    .D2(controlled_buffer_9_out[2]), .D1(controlled_buffer_9_out[1]), .D0(controlled_buffer_9_out[0]),
    .Q7(n8_bit_register_7_q0[7]), .Q6(n8_bit_register_7_q0[6]), .Q5(n8_bit_register_7_q0[5]),
    .Q4(n8_bit_register_7_q0[4]), .Q3(n8_bit_register_7_q0[3]), .Q2(n8_bit_register_7_q0[2]),
    .Q1(n8_bit_register_7_q0[1]), .Q0(n8_bit_register_7_q0[0]));
  _8_bit_register u_8_bit_register_8 (
    .CLK(and_8_out), .D7(controlled_buffer_10_out[7]), .D6(controlled_buffer_10_out[6]),
    .D5(controlled_buffer_10_out[5]), .D4(controlled_buffer_10_out[4]), .D3(controlled_buffer_10_out[3]),
    .D2(controlled_buffer_10_out[2]), .D1(controlled_buffer_10_out[1]), .D0(controlled_buffer_10_out[0]),
    .Q7(n8_bit_register_8_q0[7]), .Q6(n8_bit_register_8_q0[6]), .Q5(n8_bit_register_8_q0[5]),
    .Q4(n8_bit_register_8_q0[4]), .Q3(n8_bit_register_8_q0[3]), .Q2(n8_bit_register_8_q0[2]),
    .Q1(n8_bit_register_8_q0[1]), .Q0(n8_bit_register_8_q0[0]));
  _8_bit_register u_8_bit_register_9 (
    .CLK(and_9_out), .D7(controlled_buffer_11_out[7]), .D6(controlled_buffer_11_out[6]),
    .D5(controlled_buffer_11_out[5]), .D4(controlled_buffer_11_out[4]), .D3(controlled_buffer_11_out[3]),
    .D2(controlled_buffer_11_out[2]), .D1(controlled_buffer_11_out[1]), .D0(controlled_buffer_11_out[0]),
    .Q7(n8_bit_register_9_q0[7]), .Q6(n8_bit_register_9_q0[6]), .Q5(n8_bit_register_9_q0[5]),
    .Q4(n8_bit_register_9_q0[4]), .Q3(n8_bit_register_9_q0[3]), .Q2(n8_bit_register_9_q0[2]),
    .Q1(n8_bit_register_9_q0[1]), .Q0(n8_bit_register_9_q0[0]));
  assign controlled_buffer_12_out = and_10_out ? controlled_buffer_22_out : 8'bz;  // Controlled_Buffer controlled_buffer_12
  _8_bit_register u_8_bit_register_10 (
    .CLK(and_10_out), .D7(controlled_buffer_12_out[7]), .D6(controlled_buffer_12_out[6]),
    .D5(controlled_buffer_12_out[5]), .D4(controlled_buffer_12_out[4]), .D3(controlled_buffer_12_out[3]),
    .D2(controlled_buffer_12_out[2]), .D1(controlled_buffer_12_out[1]), .D0(controlled_buffer_12_out[0]),
    .Q7(n8_bit_register_10_q7), .Q6(n8_bit_register_10_q6), .Q5(n8_bit_register_10_q5),
    .Q4(n8_bit_register_10_q4), .Q3(n8_bit_register_10_q3), .Q2(n8_bit_register_10_q2),
    .Q1(n8_bit_register_10_q1), .Q0(n8_bit_register_10_q0));
  and and_8 (and_8_out, Clk, TOS);
  and and_9 (and_9_out, Clk, OPC);
  assign controlled_buffer_13_out = decoder_1_out0 ? out_24 : 8'bz;  // Controlled_Buffer controlled_buffer_13
  assign controlled_buffer_13_out = decoder_1_out1 ? n8_bit_register_3_q0 : 8'bz;  // Controlled_Buffer controlled_buffer_14
  assign controlled_buffer_13_out = decoder_1_out2 ? n8_bit_register_4_q0 : 8'bz;  // Controlled_Buffer controlled_buffer_15
  assign controlled_buffer_13_out = decoder_1_out3 ? n8_bit_register_5_q0 : 8'bz;  // Controlled_Buffer controlled_buffer_16
  assign controlled_buffer_13_out = decoder_1_out4 ? n8_bit_register_6_q0 : 8'bz;  // Controlled_Buffer controlled_buffer_17
  assign controlled_buffer_13_out = decoder_1_out5 ? n8_bit_register_7_q0 : 8'bz;  // Controlled_Buffer controlled_buffer_18
  assign controlled_buffer_13_out = decoder_1_out6 ? n8_bit_register_8_q0 : 8'bz;  // Controlled_Buffer controlled_buffer_19
  assign controlled_buffer_13_out = decoder_1_out7 ? n8_bit_register_9_q0 : 8'bz;  // Controlled_Buffer controlled_buffer_20
  and and_10 (and_10_out, Clk, H);
  ALU alu_1 (
    .ENB(ENB), .ENA(ENA), .INVA(INVA), .Carry_In(Cin), .F1(F1), .Clk(Clk), .Carry_Out(Carry_out), .F0(F0),
    .B7(controlled_buffer_13_out[7]), .B6(controlled_buffer_13_out[6]), .B5(controlled_buffer_13_out[5]),
    .B4(controlled_buffer_13_out[4]), .B3(controlled_buffer_13_out[3]), .B2(controlled_buffer_13_out[2]),
    .B1(controlled_buffer_13_out[1]), .B0(controlled_buffer_13_out[0]), .A7(n8_bit_register_10_q7),
    .A6(n8_bit_register_10_q6), .A5(n8_bit_register_10_q5), .A4(n8_bit_register_10_q4),
    .A3(n8_bit_register_10_q3), .A2(n8_bit_register_10_q2), .A1(n8_bit_register_10_q1),
    .A0(n8_bit_register_10_q0), .C7(alu_1_c0[7]), .C6(alu_1_c0[6]), .C5(alu_1_c0[5]), .C4(alu_1_c0[4]),
    .C3(alu_1_c0[3]), .C2(alu_1_c0[2]), .C1(alu_1_c0[1]), .C0(alu_1_c0[0]));
  assign controlled_buffer_21_out = ENS ? alu_1_c0 : 8'bz;  // Controlled_Buffer controlled_buffer_21
  not not_2 (not_2_out, ENS);
  assign controlled_buffer_22_out = not_2_out ? alu_1_c0 : 8'bz;  // Controlled_Buffer controlled_buffer_22
  assign controlled_buffer_22_out = ENS ? n8_bit_wide_1_bit_left_right_shifter_1_s0 : 8'bz;  // Controlled_Buffer controlled_buffer_23
  Decoder #(.select(3)) decoder_1 (
    .out0(decoder_1_out0), .out1(decoder_1_out1), .out2(decoder_1_out2), .out3(decoder_1_out3),
    .out4(decoder_1_out4), .out5(decoder_1_out5), .out6(decoder_1_out6), .out7(decoder_1_out7), .sel(B_Bus),
    .en(Clk));
  _8_Bit_wide__1_bit_Left_Right_Shifter u_8_bit_wide_1_bit_left_right_shifter_1 (
    .C(LRS), .D0(controlled_buffer_21_out[0]), .D1(controlled_buffer_21_out[1]),
    .D2(controlled_buffer_21_out[2]), .D3(controlled_buffer_21_out[3]), .D4(controlled_buffer_21_out[4]),
    .D5(controlled_buffer_21_out[5]), .D6(controlled_buffer_21_out[6]), .D7(controlled_buffer_21_out[7]),
    .S0(n8_bit_wide_1_bit_left_right_shifter_1_s0[0]), .S1(n8_bit_wide_1_bit_left_right_shifter_1_s0[1]),
    .S2(n8_bit_wide_1_bit_left_right_shifter_1_s0[2]), .S3(n8_bit_wide_1_bit_left_right_shifter_1_s0[3]),
    .S4(n8_bit_wide_1_bit_left_right_shifter_1_s0[4]), .S5(n8_bit_wide_1_bit_left_right_shifter_1_s0[5]),
    .S6(n8_bit_wide_1_bit_left_right_shifter_1_s0[6]), .S7(n8_bit_wide_1_bit_left_right_shifter_1_s0[7]));

  // Notes on the sheet:
  //   MAR
  //   MDR
  //   PC
  //   MBR
  //   SP
  //   LV
  //   CPP
  //   TOS
  //   OPC
  //   H
  //   3 to 8 Decoder
endmodule
