// Logisim project Latches.circ as structural Verilog: 8 circuits, main circuit SR-Latch
module SR_Latch (
  input  NOT_S,
  input  NOT_R,
  output Q,
  output NOT_Q
);

  nand nand_1 (Q, NOT_S, NOT_Q);
  nand nand_2 (NOT_Q, Q, NOT_R);
endmodule

module SR_Flip_Flop (
  input  S,
  input  CK,
  input  R,
  output Q,
  output NOT_Q
);

  wire nand_1_out, nand_2_out;

  nand nand_1 (nand_1_out, S, CK);
  nand nand_2 (nand_2_out, CK, R);
  SR_Latch SR_L (.NOT_S(nand_1_out), .NOT_R(nand_2_out), .Q(Q), .NOT_Q(NOT_Q));
endmodule

module D_Flip_Flop (
  input  D,
  input  CLK,
  output Q,
  output NOT_Q
);

  wire not_1_out;

  not not_1 (not_1_out, D);
  SR_Flip_Flop SR_FF (.S(D), .CK(CLK), .R(not_1_out), .Q(Q), .NOT_Q(NOT_Q));
endmodule

module _8_bit_register (
  input  D7,
  input  D6,
  input  D5,
  input  D4,
  input  D3,
  input  D2,
  input  D1,
  input  D0,
  input  CLK,
  output Q7,
  output Q6,
  output Q5,
  output Q4,
  output Q3,
  output Q2,
  output Q1,
  output Q0
);

  D_Flip_Flop d_flip_flop_1 (.D(D7), .CLK(CLK), .Q(Q7));  // open: NOT_Q
  D_Flip_Flop d_flip_flop_2 (.D(D6), .CLK(CLK), .Q(Q6));  // open: NOT_Q
  D_Flip_Flop d_flip_flop_3 (.D(D4), .CLK(CLK), .Q(Q4));  // open: NOT_Q
  D_Flip_Flop d_flip_flop_4 (.D(D5), .CLK(CLK), .Q(Q5));  // open: NOT_Q
  D_Flip_Flop d_flip_flop_5 (.D(D3), .CLK(CLK), .Q(Q3));  // open: NOT_Q
  D_Flip_Flop d_flip_flop_6 (.D(D2), .CLK(CLK), .Q(Q2));  // open: NOT_Q
  D_Flip_Flop d_flip_flop_7 (.D(D1), .CLK(CLK), .Q(Q1));  // open: NOT_Q
  D_Flip_Flop d_flip_flop_8 (.D(D0), .CLK(CLK), .Q(Q0));  // open: NOT_Q
endmodule

module Binary_Memory_Cell (
  input  Select,
  input  Data_In,
  input  Read_1___Write_0,
  output Data_Out
);

  wire and_1_out, and_2_out, not_1_out, not_2_out, not_3_out, not_4_out, SR_Latch_q;

  not not_1 (not_1_out, Data_In);
  and and_1 (and_1_out, Select, Data_In, not_4_out);
  not not_2 (not_2_out, and_1_out);
  not not_3 (not_3_out, and_2_out);
  and and_2 (and_2_out, Select, not_1_out, not_4_out);
  not not_4 (not_4_out, Read_1___Write_0);
  SR_Latch SR_Latch (.NOT_S(not_2_out), .NOT_R(not_3_out), .Q(SR_Latch_q));  // open: NOT_Q
  and and_3 (Data_Out, Select, SR_Latch_q, Read_1___Write_0);

  // Notes on the sheet:
  //   Binary Memory Cell
  //   S
  //   R
  //   Q
endmodule

module Single_Bit_Memory_Cell (
  input  Data_Bus_Input,
  input  [1:0] Control_Bus_Input,
  output Data_Bus_State,
  output [1:0] Control_Line_State
);

  wire binary_memory_cell_1_data_out, controlled_buffer_2_out, not_1_out;

  assign Data_Bus_State = not_1_out ? Data_Bus_Input : 1'bz;  // Controlled_Buffer controlled_buffer_1
  not not_1 (not_1_out, Control_Bus_Input[1]);
  assign controlled_buffer_2_out = not_1_out ? Data_Bus_State : 1'bz;  // Controlled_Buffer controlled_buffer_2
  Binary_Memory_Cell binary_memory_cell_1 (
    .Data_In(controlled_buffer_2_out), .Data_Out(binary_memory_cell_1_data_out),
    .Select(Control_Bus_Input[0]), .Read_1___Write_0(Control_Bus_Input[1]));
  assign Data_Bus_State = Control_Bus_Input[1] ? binary_memory_cell_1_data_out : 1'bz;  // Controlled_Buffer controlled_buffer_3

  assign Control_Line_State = Control_Bus_Input;
endmodule

module _8_Bit_Memory_Cell (
  input  Enable,
  input  Read_1___Write_0,
  input  in_3,
  input  in_4,
  input  in_5,
  input  in_6,
  input  in_7,
  input  in_8,
  input  in_9,
  input  in_10,
  output out_11,
  output out_12,
  output out_13,
  output out_14,
  output out_15,
  output out_16,
  output out_17,
  output out_18
);

  Binary_Memory_Cell binary_memory_cell_1 (
    .Data_In(in_3), .Data_Out(out_11), .Select(Enable), .Read_1___Write_0(Read_1___Write_0));
  Binary_Memory_Cell binary_memory_cell_2 (
    .Data_In(in_4), .Data_Out(out_12), .Select(Enable), .Read_1___Write_0(Read_1___Write_0));
  Binary_Memory_Cell binary_memory_cell_3 (
    .Data_In(in_5), .Data_Out(out_13), .Select(Enable), .Read_1___Write_0(Read_1___Write_0));
  Binary_Memory_Cell binary_memory_cell_4 (
    .Data_In(in_6), .Data_Out(out_14), .Select(Enable), .Read_1___Write_0(Read_1___Write_0));
  Binary_Memory_Cell binary_memory_cell_5 (
    .Data_In(in_7), .Data_Out(out_15), .Select(Enable), .Read_1___Write_0(Read_1___Write_0));
  Binary_Memory_Cell binary_memory_cell_6 (
    .Data_In(in_8), .Data_Out(out_16), .Select(Enable), .Read_1___Write_0(Read_1___Write_0));
  Binary_Memory_Cell binary_memory_cell_7 (
    .Data_In(in_9), .Data_Out(out_17), .Select(Enable), .Read_1___Write_0(Read_1___Write_0));
  Binary_Memory_Cell binary_memory_cell_8 (
    .Data_In(in_10), .Data_Out(out_18), .Select(Enable), .Read_1___Write_0(Read_1___Write_0));
endmodule

module _4_Byte_Addressable_Memory_Chip (
  input  [7:0] in_1,
  input  [7:0] in_2,
  input  [1:0] in_3,
  output [7:0] _8_Bit_Data_Bus,
  output [7:0] _8_Bit_Address_Bus,
  output [1:0] out_6
);

  wire Address_Decoder_a___b, Address_Decoder_a___not_b, Address_Decoder_not_a___b,
       Address_Decoder_not_a___not_b, and_1_out, and_2_out, n8_bit_memory_cell_1_out_11,
       n8_bit_memory_cell_1_out_12, n8_bit_memory_cell_1_out_13, n8_bit_memory_cell_1_out_14,
       n8_bit_memory_cell_1_out_15, n8_bit_memory_cell_1_out_16, n8_bit_memory_cell_1_out_17,
       n8_bit_memory_cell_1_out_18, n8_bit_memory_cell_2_out_11, n8_bit_memory_cell_2_out_12,
       n8_bit_memory_cell_2_out_13, n8_bit_memory_cell_2_out_14, n8_bit_memory_cell_2_out_15,
       n8_bit_memory_cell_2_out_16, n8_bit_memory_cell_2_out_17, n8_bit_memory_cell_2_out_18,
       n8_bit_memory_cell_3_out_11, n8_bit_memory_cell_3_out_12, n8_bit_memory_cell_3_out_13,
       n8_bit_memory_cell_3_out_14, n8_bit_memory_cell_3_out_15, n8_bit_memory_cell_3_out_16,
       n8_bit_memory_cell_3_out_17, n8_bit_memory_cell_3_out_18, n8_bit_memory_cell_4_out_11,
       n8_bit_memory_cell_4_out_12, n8_bit_memory_cell_4_out_13, n8_bit_memory_cell_4_out_14,
       n8_bit_memory_cell_4_out_15, n8_bit_memory_cell_4_out_16, n8_bit_memory_cell_4_out_17,
       n8_bit_memory_cell_4_out_18, not_1_out, not_2_out, or_1_out;
  wire [7:0] controlled_buffer_2_out, D0_out;

  and and_1 (and_1_out, not_1_out, in_3[0]);
  not not_1 (not_1_out, or_1_out);
  and and_2 (and_2_out, in_3[1], in_3[0]);
  _2to4Decoder Address_Decoder (
    .A(in_2[1]), .B(in_2[0]), .Enable(and_1_out), .NOT_A___NOT_B(Address_Decoder_not_a___not_b),
    .A___NOT_B(Address_Decoder_a___not_b), .NOT_A___B(Address_Decoder_not_a___b),
    .A___B(Address_Decoder_a___b));
  or or_1 (or_1_out, in_2[7], in_2[6], in_2[5], in_2[4], in_2[3], in_2[2]);
  assign _8_Bit_Data_Bus = not_2_out ? in_1 : 8'bz;  // Controlled_Buffer controlled_buffer_1
  assign controlled_buffer_2_out = not_2_out ? _8_Bit_Data_Bus : 8'bz;  // Controlled_Buffer controlled_buffer_2
  not not_2 (not_2_out, and_2_out);
  _8_Bit_Memory_Cell u_8_bit_memory_cell_1 (
    .in_3(controlled_buffer_2_out[0]), .in_4(controlled_buffer_2_out[1]), .in_5(controlled_buffer_2_out[2]),
    .in_6(controlled_buffer_2_out[3]), .in_7(controlled_buffer_2_out[4]), .in_8(controlled_buffer_2_out[5]),
    .in_9(controlled_buffer_2_out[6]), .in_10(controlled_buffer_2_out[7]),
    .Enable(Address_Decoder_not_a___not_b), .Read_1___Write_0(in_3[1]), .out_11(n8_bit_memory_cell_1_out_11),
    .out_12(n8_bit_memory_cell_1_out_12), .out_13(n8_bit_memory_cell_1_out_13),
    .out_14(n8_bit_memory_cell_1_out_14), .out_15(n8_bit_memory_cell_1_out_15),
    .out_16(n8_bit_memory_cell_1_out_16), .out_17(n8_bit_memory_cell_1_out_17),
    .out_18(n8_bit_memory_cell_1_out_18));
  _8_Bit_Memory_Cell u_8_bit_memory_cell_2 (
    .in_3(controlled_buffer_2_out[0]), .in_4(controlled_buffer_2_out[1]), .in_5(controlled_buffer_2_out[2]),
    .in_6(controlled_buffer_2_out[3]), .in_7(controlled_buffer_2_out[4]), .in_8(controlled_buffer_2_out[5]),
    .in_9(controlled_buffer_2_out[6]), .in_10(controlled_buffer_2_out[7]),
    .Enable(Address_Decoder_a___not_b), .Read_1___Write_0(in_3[1]), .out_11(n8_bit_memory_cell_2_out_11),
    .out_12(n8_bit_memory_cell_2_out_12), .out_13(n8_bit_memory_cell_2_out_13),
    .out_14(n8_bit_memory_cell_2_out_14), .out_15(n8_bit_memory_cell_2_out_15),
    .out_16(n8_bit_memory_cell_2_out_16), .out_17(n8_bit_memory_cell_2_out_17),
    .out_18(n8_bit_memory_cell_2_out_18));
  _8_Bit_Memory_Cell u_8_bit_memory_cell_3 (
    .in_3(controlled_buffer_2_out[0]), .in_4(controlled_buffer_2_out[1]), .in_5(controlled_buffer_2_out[2]),
    .in_6(controlled_buffer_2_out[3]), .in_7(controlled_buffer_2_out[4]), .in_8(controlled_buffer_2_out[5]),
    .in_9(controlled_buffer_2_out[6]), .in_10(controlled_buffer_2_out[7]),
    .Enable(Address_Decoder_not_a___b), .Read_1___Write_0(in_3[1]), .out_11(n8_bit_memory_cell_3_out_11),
    .out_12(n8_bit_memory_cell_3_out_12), .out_13(n8_bit_memory_cell_3_out_13),
    .out_14(n8_bit_memory_cell_3_out_14), .out_15(n8_bit_memory_cell_3_out_15),
    .out_16(n8_bit_memory_cell_3_out_16), .out_17(n8_bit_memory_cell_3_out_17),
    .out_18(n8_bit_memory_cell_3_out_18));
  _8_Bit_Memory_Cell u_8_bit_memory_cell_4 (
    .in_3(controlled_buffer_2_out[0]), .in_4(controlled_buffer_2_out[1]), .in_5(controlled_buffer_2_out[2]),
    .in_6(controlled_buffer_2_out[3]), .in_7(controlled_buffer_2_out[4]), .in_8(controlled_buffer_2_out[5]),
    .in_9(controlled_buffer_2_out[6]), .in_10(controlled_buffer_2_out[7]), .Enable(Address_Decoder_a___b),
    .Read_1___Write_0(in_3[1]), .out_11(n8_bit_memory_cell_4_out_11), .out_12(n8_bit_memory_cell_4_out_12),
    .out_13(n8_bit_memory_cell_4_out_13), .out_14(n8_bit_memory_cell_4_out_14),
    .out_15(n8_bit_memory_cell_4_out_15), .out_16(n8_bit_memory_cell_4_out_16),
    .out_17(n8_bit_memory_cell_4_out_17), .out_18(n8_bit_memory_cell_4_out_18));
  or D7 (D0_out[7], n8_bit_memory_cell_4_out_18, n8_bit_memory_cell_3_out_18, n8_bit_memory_cell_2_out_18, n8_bit_memory_cell_1_out_18);
  or D6 (D0_out[6], n8_bit_memory_cell_4_out_17, n8_bit_memory_cell_3_out_17, n8_bit_memory_cell_2_out_17, n8_bit_memory_cell_1_out_17);
  or D5 (D0_out[5], n8_bit_memory_cell_4_out_16, n8_bit_memory_cell_3_out_16, n8_bit_memory_cell_2_out_16, n8_bit_memory_cell_1_out_16);
  or D4 (D0_out[4], n8_bit_memory_cell_4_out_15, n8_bit_memory_cell_3_out_15, n8_bit_memory_cell_2_out_15, n8_bit_memory_cell_1_out_15);
  or D3 (D0_out[3], n8_bit_memory_cell_4_out_14, n8_bit_memory_cell_3_out_14, n8_bit_memory_cell_2_out_14, n8_bit_memory_cell_1_out_14);
  or D1 (D0_out[1], n8_bit_memory_cell_4_out_12, n8_bit_memory_cell_3_out_12, n8_bit_memory_cell_2_out_12, n8_bit_memory_cell_1_out_12);
  or D2 (D0_out[2], n8_bit_memory_cell_4_out_13, n8_bit_memory_cell_3_out_13, n8_bit_memory_cell_2_out_13, n8_bit_memory_cell_1_out_13);
  or D0 (D0_out[0], n8_bit_memory_cell_4_out_11, n8_bit_memory_cell_3_out_11, n8_bit_memory_cell_2_out_11, n8_bit_memory_cell_1_out_11);
  assign _8_Bit_Data_Bus = and_2_out ? D0_out : 8'bz;  // Controlled_Buffer controlled_buffer_3

  assign _8_Bit_Address_Bus = in_2;
  assign out_6 = in_3;

  // Notes on the sheet:
  //   Chip Select Address
  //   Chip Select Address
  //   Memory Cell Input
endmodule
